# Fritzing sketch TempLogger (saved by Fritzing 0.9.2b)
breadboards: 1

parts:
  RHT1 = Humidity and Temperature Sensor RHT03
  U1 = ESP8266 WiFi Module [part_number=ESP8266]
  R1 = Resistor [tolerance=±5% resistance=10k package=THT]
  Power_plug1 = Power plug
  S1 = Pushbutton [package="[SMD]"]
  LED1 = LED - 3mm [color="Red (633nm)" package="3 mm [THT]"]
  R2 = Resistor [tolerance=±5% resistance=220 package="0402 [SMD]"]

nets:
  3.3V: RHT1.Vcc, U1.VCC, R1.Pin_0, Power_plug1.VCC
  N1: RHT1.Data-signal, U1.GPIO_2, R1.Pin_1
  GND: RHT1.GND_2, U1.GND, Power_plug1.GND, S1.Pin_3, S1.Pin_4, LED1.cathode
  N2: U1.GPIO_4, R2.Pin_1
  N3: U1.GPIO_13, S1.Pin_1, S1.Pin_2
  N4: LED1.anode, R2.Pin_0

custom parts:
  ESP8266 WiFi Module: Generic WiFi Module based on the ESP8266 with onboard PCB antenna and UART communications
